# Fritzing sketch wiring-diagram (saved by Fritzing 0.9.6b)
breadboards: 1

parts:
  Raspberry_Pi_Zero_W = Raspberry Pi Zero
  LCD1 = LCD screen
  S2 = Pushbutton [package="[SMD]"]
  R1 = Resistor [tolerance=±5% resistance=1k power=0.25 package=THT]
  U3 = POT [package=trim_pot]
  8_Channel_Relay1 = 8 Channel Power Relay
  R4 = Resistor [tolerance=±5% resistance=1k power=0.25 package=THT]
  LED1 = LEDs [package=led10mm]  # not connected

nets:
  VDD: Raspberry_Pi_Zero_W.pin_2, Raspberry_Pi_Zero_W.pin_4, LCD1.VDD, 8_Channel_Relay1.VCC
  N1: Raspberry_Pi_Zero_W.pin_5, S2.Pin_3, S2.Pin_4, R1.Pin_0
  VSS: Raspberry_Pi_Zero_W.pin_6, Raspberry_Pi_Zero_W.pin_9, Raspberry_Pi_Zero_W.pin_34, Raspberry_Pi_Zero_W.pin_39, LCD1.VSS, LCD1.R/W, LCD1.LED-, S2.Pin_1, S2.Pin_2, R1.Pin_1, U3.S, 8_Channel_Relay1.GND
  N2: Raspberry_Pi_Zero_W.pin_18, R4.Pin_1
  N3: Raspberry_Pi_Zero_W.pin_21, LCD1.LED+
  N4: Raspberry_Pi_Zero_W.pin_22, 8_Channel_Relay1.IN1
  N5: Raspberry_Pi_Zero_W.pin_24, 8_Channel_Relay1.IN2
  N6: Raspberry_Pi_Zero_W.pin_26, 8_Channel_Relay1.IN3
  N7: Raspberry_Pi_Zero_W.pin_27, LCD1.DB7
  N8: Raspberry_Pi_Zero_W.pin_28, 8_Channel_Relay1.IN4
  N9: Raspberry_Pi_Zero_W.pin_29, LCD1.DB6
  N10: Raspberry_Pi_Zero_W.pin_31, LCD1.DB5
  N11: Raspberry_Pi_Zero_W.pin_33, LCD1.DB4
  N12: Raspberry_Pi_Zero_W.pin_35, LCD1.E
  N13: Raspberry_Pi_Zero_W.pin_37, LCD1.RS
  N14: LCD1.V0, U3.E

custom parts:
  8 Channel Power Relay: An 8 channel power relay. The module operates at 5V.
